// Logisim project Project File.circ as structural Verilog: 1 circuit, main circuit main
module main (
  input  D,
  input  in_2,
  input  in_3,
  input  in_4,
  input  in_5,
  input  B,
  input  C,
  output out_8,
  output out_9,
  output out_10,
  output out_11,
  output out_12,
  output out_13,
  output out_14,
  output out_15,
  output out_16
);

  wire and_1_out, and_2_out, and_3_out, and_4_out, and_5_out, and_6_out, clock_1_out, clock_2_out, d_ff_1_q,
       d_ff_2_q, d_ff_3_q, j_k_ff_1_qn, j_k_ff_2_qn, j_k_ff_3_qn, j_k_ff_4_qn, j_k_ff_5_qn, j_k_ff_6_qn,
       not_1_out, not_2_out, or_1_out, or_2_out, or_3_out;

  Clock clock_1 (.out(clock_1_out));
  not not_1 (not_1_out, in_5);
  and and_1 (and_1_out, d_ff_3_q, in_5);
  and and_2 (and_2_out, not_1_out, D);
  D_Flip_Flop d_ff_1 (.clk(clock_1_out), .D(in_2), .Q(d_ff_1_q), .reset(in_3));  // open: Qn, preset, en
  and and_3 (and_3_out, d_ff_1_q, in_5);
  and and_4 (and_4_out, not_1_out, B);
  or or_1 (or_1_out, and_1_out, and_2_out);
  D_Flip_Flop d_ff_2 (.clk(clock_1_out), .D(or_2_out), .Q(d_ff_2_q), .reset(in_3));  // open: Qn, preset, en
  or or_2 (or_2_out, and_3_out, and_4_out);
  and and_5 (and_5_out, d_ff_2_q, in_5);
  and and_6 (and_6_out, not_1_out, C);
  D_Flip_Flop d_ff_3 (.clk(clock_1_out), .D(or_3_out), .Q(d_ff_3_q), .reset(in_3));  // open: Qn, preset, en
  D_Flip_Flop d_ff_4 (.clk(clock_1_out), .D(or_1_out), .Q(out_12), .reset(in_3));  // open: Qn, preset, en
  or or_3 (or_3_out, and_5_out, and_6_out);
  Clock clock_2 (.out(clock_2_out));
  not not_2 (not_2_out, out_12);
  J_K_Flip_Flop j_k_ff_1 (
    .J(out_12), .clk(clock_2_out), .K(out_12), .Q(out_8), .Qn(j_k_ff_1_qn), .reset(in_4));  // open: preset, en
  J_K_Flip_Flop j_k_ff_2 (
    .J(out_12), .clk(j_k_ff_1_qn), .K(out_12), .Q(out_9), .Qn(j_k_ff_2_qn), .reset(in_4));  // open: preset, en
  J_K_Flip_Flop j_k_ff_3 (
    .J(not_2_out), .clk(clock_2_out), .K(not_2_out), .Q(out_13), .Qn(j_k_ff_3_qn), .reset(in_4));  // open: preset, en
  J_K_Flip_Flop j_k_ff_4 (
    .J(out_12), .clk(j_k_ff_2_qn), .K(out_12), .Q(out_10), .Qn(j_k_ff_4_qn), .reset(in_4));  // open: preset, en
  J_K_Flip_Flop j_k_ff_5 (
    .J(not_2_out), .clk(j_k_ff_3_qn), .K(not_2_out), .Q(out_14), .Qn(j_k_ff_5_qn), .reset(in_4));  // open: preset, en
  J_K_Flip_Flop j_k_ff_6 (
    .J(not_2_out), .clk(j_k_ff_5_qn), .K(not_2_out), .Q(out_15), .Qn(j_k_ff_6_qn), .reset(in_4));  // open: preset, en
  J_K_Flip_Flop j_k_ff_7 (.J(out_12), .clk(j_k_ff_4_qn), .K(out_12), .Q(out_11), .reset(in_4));  // open: Qn, preset, en
  J_K_Flip_Flop j_k_ff_8 (
    .J(not_2_out), .clk(j_k_ff_6_qn), .K(not_2_out), .Q(out_16), .reset(in_4));  // open: Qn, preset, en

  // Notes on the sheet:
  //   A
  //   Clear
  //   A=0 Load
  //   = 1 Shift
  //   1's Count
  //   0's Count
  //   Clear
endmodule
