// Logisim project Project Using Magnitude Comparator.circ as structural Verilog: 1 circuit, main circuit main
module main (
  input  in_1,
  input  in_2,
  output out_3,
  output out_4,
  output out_5,
  output out_6,
  output out_7,
  output out_8,
  output out_9,
  output out_10,
  output out_11,
  output out_12,
  output out_13
);

  wire clock_1_out, clock_2_out, j_k_ff_1_qn, j_k_ff_2_qn, j_k_ff_3_qn, j_k_ff_5_qn, j_k_ff_6_qn,
       j_k_ff_7_qn, not_1_out, not_2_out;

  Clock clock_1 (.out(clock_1_out));
  J_K_Flip_Flop j_k_ff_1 (
    .J(out_7), .clk(clock_1_out), .K(out_7), .Q(out_3), .Qn(j_k_ff_1_qn));  // open: preset, en, reset
  not not_1 (not_1_out, in_1);
  not not_2 (not_2_out, in_2);
  J_K_Flip_Flop j_k_ff_2 (
    .J(out_7), .clk(j_k_ff_1_qn), .K(out_7), .Q(out_4), .Qn(j_k_ff_2_qn));  // open: preset, en, reset
  and and_1 (out_7, not_1_out, in_2);
  and and_2 (out_9, in_1, not_2_out);
  J_K_Flip_Flop j_k_ff_3 (
    .J(out_7), .clk(j_k_ff_2_qn), .K(out_7), .Q(out_5), .Qn(j_k_ff_3_qn));  // open: preset, en, reset
  Clock clock_2 (.out(clock_2_out));
  J_K_Flip_Flop j_k_ff_4 (.J(out_7), .clk(j_k_ff_3_qn), .K(out_7), .Q(out_6));  // open: Qn, preset, en, reset
  nor nor_1 (out_8, out_7, out_9);
  J_K_Flip_Flop j_k_ff_5 (
    .J(out_8), .clk(clock_2_out), .K(out_8), .Q(out_10), .Qn(j_k_ff_5_qn));  // open: preset, en, reset
  J_K_Flip_Flop j_k_ff_6 (
    .J(out_8), .clk(j_k_ff_5_qn), .K(out_8), .Q(out_11), .Qn(j_k_ff_6_qn));  // open: preset, en, reset
  J_K_Flip_Flop j_k_ff_7 (
    .J(out_8), .clk(j_k_ff_6_qn), .K(out_8), .Q(out_12), .Qn(j_k_ff_7_qn));  // open: preset, en, reset
  J_K_Flip_Flop j_k_ff_8 (.J(out_8), .clk(j_k_ff_7_qn), .K(out_8), .Q(out_13));  // open: Qn, preset, en, reset
endmodule
